// Logisim project TinyCPU-Peripherals.circ as structural Verilog: 4 circuits, main circuit TinyCPUSystemMain
module TinyCPUSystemMain (
  input  CLK,
  input  RESET,
  input  INTERRUPT_REQUEST,
  output [15:0] OUTPUT_PORT_VALUE,
  output OUTPUT_PORT_VALID,
  output INTERRUPT_ENABLED,
  output INTERRUPT_PENDING,
  output IN_INTERRUPT_HANDLER,
  output [11:0] RETURN_ADDRESS,
  output RETURN_ADDRESS_VALID
);
endmodule

module OutputPort (
  input  [15:0] WRITE_VALUE,
  input  WRITE_VALID,
  input  WRITE_ENABLE,
  input  CLK,
  input  RESET,
  output [15:0] VALUE,
  output VALID
);

  Register #(.width(16)) OUTPUT_VALUE (.D(WRITE_VALUE), .en(WRITE_ENABLE), .clk(CLK), .Q(VALUE), .clr(RESET));
  Register #(.width(1)) OUTPUT_VALID (.D(WRITE_VALID), .en(WRITE_ENABLE), .clk(CLK), .Q(VALID), .clr(RESET));
endmodule

module OutputMemoryPath (
  input  [11:0] ADDRESS,
  input  [15:0] WRITE_VALUE,
  input  WRITE_VALID,
  input  WRITE_ENABLE,
  input  [15:0] RAM_READ_VALUE,
  input  RAM_READ_VALID,
  input  CLK,
  input  RESET,
  output [15:0] READ_VALUE,
  output READ_VALID,
  output RAM_WRITE_ENABLE,
  output [15:0] OUTPUT_PORT_VALUE,
  output OUTPUT_PORT_VALID
);

  wire comparator_1_eq, NOT_OUTPUT_ADDRESS_out, OUTPUT_WRITE_GATE_out;

  Comparator #(.width(12)) comparator_1 (.a({12{1'b1}}), .b(ADDRESS), .eq(comparator_1_eq));  // open: gt, lt
  not NOT_OUTPUT_ADDRESS (NOT_OUTPUT_ADDRESS_out, comparator_1_eq);
  and RAM_WRITE_GATE (RAM_WRITE_ENABLE, WRITE_VALID, NOT_OUTPUT_ADDRESS_out);
  and OUTPUT_WRITE_GATE (OUTPUT_WRITE_GATE_out, NOT_OUTPUT_ADDRESS_out, comparator_1_eq);
  Register #(.width(16)) register_1 (.D(WRITE_VALUE), .en(WRITE_ENABLE), .clk(CLK), .Q(OUTPUT_PORT_VALUE), .clr(RESET));
  Register #(.width(1)) register_2 (
    .D(WRITE_VALID), .en(OUTPUT_WRITE_GATE_out), .clk(CLK), .Q(OUTPUT_PORT_VALID), .clr(RESET));
  Multiplexer #(.width(16)) multiplexer_1 (
    .in0(RAM_READ_VALUE), .in1(OUTPUT_PORT_VALUE), .out(READ_VALUE));  // open: sel
  Multiplexer multiplexer_2 (.in0(RAM_READ_VALID), .in1(OUTPUT_PORT_VALID), .out(READ_VALID), .sel(comparator_1_eq));
endmodule

module InterruptController (
  input  INTERRUPT_REQUEST,
  input  INSTRUCTION_BOUNDARY,
  input  ENABLE_REQUEST,
  input  DISABLE_REQUEST,
  input  RETURN_REQUEST,
  input  [11:0] NEXT_PC,
  input  CLK,
  input  RESET,
  output INTERRUPT_ACCEPT,
  output [11:0] TARGET_PC,
  output INTERRUPT_ENABLED,
  output INTERRUPT_PENDING,
  output IN_INTERRUPT_HANDLER,
  output [11:0] RETURN_ADDRESS,
  output RETURN_ADDRESS_VALID,
  output ILLEGAL_RETURN
);

  wire HANDLER_HOLD_out, HANDLER_NEXT_out, INTERRUPT_ACCEPT_GATE_p1, INTERRUPT_ACCEPT_GATE_p3,
       MASK_CLEAR_NOT_out, MASK_CLEAR_REQUEST_out, PENDING_HOLD_UNTIL_ACCEPT_p1, PREVIOUS_REQUEST_NOT_out,
       register_2_p1, register_3_p2, register_4_q, REQUEST_LEVEL_q, RETURN_VALID_HOLD_out,
       RETURN_VALID_NEXT_out, RISING_EDGE_DETECT_out, undriven, undriven_2, undriven_3, undriven_4,
       undriven_5, VALID_RETURN_GATE_out, VALID_RETURN_NOT_out;

  Register #(.width(12)) register_1 (.D(NEXT_PC), .en(undriven));  // open: clk, Q, clr
  // OR_Gate PENDING_SET_OR_HOLD is placed but not wired
  // OR_Gate MASK_SET_REQUEST is placed but not wired
  // OR_Gate MASK_CLEAR_REQUEST has open pins: out=MASK_CLEAR_REQUEST_out
  Register #(.width(1)) REQUEST_LEVEL (.D(INTERRUPT_REQUEST), .en(1'b1), .Q(REQUEST_LEVEL_q));  // open: clk, clr
  // Register #(.width(1)) register_2: pin names not known; wires that end beside it: register_2_p1, 1'b1, register_2_p1
  not MASK_CLEAR_NOT (MASK_CLEAR_NOT_out, MASK_CLEAR_REQUEST_out);
  // Register #(.width(1)) register_3: pin names not known; wires that end beside it: 1'b1, register_3_p2
  Register #(.width(1)) register_4 (.Q(register_4_q));  // open: D, en, clk, clr
  Register #(.width(1)) register_5 (.en(CLK), .clr(undriven_3));  // open: D, clk, Q
  not PREVIOUS_REQUEST_NOT (PREVIOUS_REQUEST_NOT_out, REQUEST_LEVEL_q);
  // NOT_Gate NOT_IN_HANDLER has open pins: in=register_3_p2, out=open
  // AND_Gate MASK_HOLD has open pins: in0=undriven_3, in1=MASK_CLEAR_NOT_out, out=open
  and RISING_EDGE_DETECT (RISING_EDGE_DETECT_out, INTERRUPT_REQUEST, PREVIOUS_REQUEST_NOT_out);
  // AND_Gate INTERRUPT_ACCEPT_GATE: pin names not known; wires that end beside it: INTERRUPT_ACCEPT_GATE_p1, INTERRUPT_ACCEPT_GATE_p1, INTERRUPT_ACCEPT_GATE_p3
  // AND_Gate ILLEGAL_RETURN_GATE is placed but not wired
  // AND_Gate PENDING_HOLD_UNTIL_ACCEPT: pin names not known; wires that end beside it: PENDING_HOLD_UNTIL_ACCEPT_p1, PENDING_HOLD_UNTIL_ACCEPT_p1
  and VALID_RETURN_GATE (VALID_RETURN_GATE_out, RETURN_REQUEST, undriven_2, undriven);
  and RETURN_VALID_HOLD (RETURN_VALID_HOLD_out, undriven, VALID_RETURN_NOT_out);
  and HANDLER_HOLD (HANDLER_HOLD_out, undriven_2, VALID_RETURN_NOT_out);
  // NOT_Gate INTERRUPT_ACCEPT_NOT has open pins: in=INTERRUPT_ACCEPT_GATE_p3, out=open
  Multiplexer #(.width(12)) multiplexer_1 (.in0(12'hff0), .sel(undriven_4));  // open: in1, out
  // OR_Gate MASK_NEXT is placed but not wired
  not VALID_RETURN_NOT (VALID_RETURN_NOT_out, VALID_RETURN_GATE_out);
  buf HANDLER_NEXT (HANDLER_NEXT_out, HANDLER_HOLD_out);  // OR_Gate
  buf RETURN_VALID_NEXT (RETURN_VALID_NEXT_out, undriven_5);  // OR_Gate

  // Notes on the sheet:
  //   MASK NEXT STATE
  //   AP-18 interrupt state: reset > accept at instruction boundary > instruction; rising edges remain pending while masked
  //   RETURN VALID NEXT STATE
  //   HANDLER NEXT STATE
endmodule
